// Logisim project alu.circ as structural Verilog: 1 circuit, main circuit alu
module alu (
  input  alu_sub,
  input  alu_use_c,
  input  alu_cin,
  input  [7:0] alu_a,
  input  [7:0] alu_b,
  output [7:0] alu_s,
  output alu_c,
  output alu_n,
  output alu_z
);

  wire U1_pin6, U1_pin8, U1_pin12, U1_pin13, U2_pin1, U2_pin13;

  add_sub8 add_sub8_1 (
    .add_sub8_a(alu_a), .add_sub8_b(alu_b), .add_sub8_sub(alu_sub), .add_sub8_use_c(alu_use_c),
    .add_sub8_cin(alu_cin), .add_sub8_c(alu_c), .add_sub8_s({alu_n, alu_s[6:0]}));
  _7427 U1 (
    .pin1(alu_s[0]), .pin2(alu_s[1]), .pin3(alu_s[2]), .pin4(alu_s[3]), .pin5(alu_s[4]), .pin6(U1_pin6),
    .pin13(U1_pin13), .pin12(U1_pin12), .pin11(alu_n), .pin10(alu_s[6]), .pin9(alu_s[5]), .pin8(U1_pin8));
  _7411 U2 (
    .pin1(U2_pin1), .pin2(U2_pin1), .pin3(U2_pin1), .pin4(U2_pin1), .pin5(U2_pin1), .pin13(U2_pin13),
    .pin11(U1_pin12), .pin10(U1_pin6), .pin9(U1_pin8), .pin8(alu_z));  // open: pin6, pin12

  assign alu_s[7] = alu_n;
  // also tied to GND on the sheet: {U1_pin13, U2_pin13, U2_pin1}

  // Notes on the sheet:
  //   z: nor of s
  //   z: and
endmodule
